// Logisim project alu.circ as structural Verilog: 11 circuits, main circuit AND_2bit
module alu (
  input  [31:0] A,
  input  [31:0] B,
  input  [3:0] ALUSel,
  output [31:0] Result
);

  wire and_1_out;
  wire [31:0] add0, and1, bit_extender_1_out, mul10, mulh14, mulhu11, or2, sll6, slt7, sra5, srl4, xor3,
       xor_32bit_1_out_3;

  Multiplexer #(.enable("false"), .select(4), .width(32)) multiplexer_1 (
    .in0(add0), .in1(and1), .in2(or2), .in3(xor3), .in4(srl4), .in5(sra5), .in6(sll6), .in7(slt7),
    .in10(mul10), .in11(mulhu11), .in12(add0), .in13(B), .in14(mulh14), .out(Result), .sel(ALUSel));  // open: in8, in9, in15
  and and_1 (and_1_out, ALUSel[2], ALUSel[3]);
  Bit_Extender #(.in_width(1), .out_width(32), .\type ("input")) bit_extender_1 (
    .in(and_1_out), .out(bit_extender_1_out));  // open: extend
  XOR_32bit xor_32bit_1 (.in_1(bit_extender_1_out), .in_2(B), .out_3(xor_32bit_1_out_3));
  Adder #(.width(32)) adder_1 (.a(A), .b(xor_32bit_1_out_3), .out(add0), .cin(and_1_out));  // open: cout
  Shifter #(.shift("lr"), .width(32)) shifter_1 (.in(A), .\dist (B[4:0]), .out(srl4));
  Shifter #(.shift("ar"), .width(32)) shifter_2 (.in(A), .\dist (B[4:0]), .out(sra5));
  Shifter #(.width(32)) shifter_3 (.in(A), .\dist (B[4:0]), .out(sll6));
  Multiplier #(.mode("twosComplement"), .width(32)) multiplier_1 (
    .a(A), .b(B), .out(mul10), .cout(mulh14));  // open: cin
  Multiplier #(.width(32)) multiplier_2 (.a(A), .b(B), .cout(mulhu11));  // open: out, cin
  AND_32bit and_32bit_1 (.in_1(A), .in_2(B), .out_3(and1));
  OR_32bit or_32bit_1 (.in_1(A), .in_2(B), .out_3(or2));
  XOR_32bit xor_32bit_2 (.in_1(A), .in_2(B), .out_3(xor3));
  slt slt_1 (.in_1(A), .in_2(B), .out_3(slt7));

  // Other names for the same wires on the sheet: bsel13[31:0] = B; sub12[31:0] = add0

  // Notes on the sheet:
  //   INPUTS to your circuit
  //   DON'T CHANGE THE LOCATIONS OF THE INPUTS AND OUTPUTS!
  //   OUTPUT from your circuit
endmodule

module AND_2bit (
  input  [1:0] in_1,
  input  [1:0] in_2,
  output [1:0] out_3
);

  and and_1 (out_3[0], in_1[0], in_2[0]);
  and and_2 (out_3[1], in_1[1], in_2[1]);
endmodule

module AND_8bit (
  input  [7:0] in_1,
  input  [7:0] in_2,
  output [7:0] out_3
);

  AND_2bit and_2bit_1 (.in_1(in_1[1:0]), .in_2(in_2[1:0]), .out_3(out_3[1:0]));
  AND_2bit and_2bit_2 (.in_1(in_1[3:2]), .in_2(in_2[3:2]), .out_3(out_3[3:2]));
  AND_2bit and_2bit_3 (.in_1(in_1[5:4]), .in_2(in_2[5:4]), .out_3(out_3[5:4]));
  AND_2bit and_2bit_4 (.in_1(in_1[7:6]), .in_2(in_2[7:6]), .out_3(out_3[7:6]));
endmodule

module AND_32bit (
  input  [31:0] in_1,
  input  [31:0] in_2,
  output [31:0] out_3
);

  AND_8bit and_8bit_1 (.in_1(in_1[7:0]), .in_2(in_2[7:0]), .out_3(out_3[7:0]));
  AND_8bit and_8bit_2 (.in_1(in_1[15:8]), .in_2(in_2[15:8]), .out_3(out_3[15:8]));
  AND_8bit and_8bit_3 (.in_1(in_1[23:16]), .in_2(in_2[23:16]), .out_3(out_3[23:16]));
  AND_8bit and_8bit_4 (.in_1(in_1[31:24]), .in_2(in_2[31:24]), .out_3(out_3[31:24]));
endmodule

module OR_2bit (
  input  [1:0] in_1,
  input  [1:0] in_2,
  output [1:0] out_3
);

  or or_1 (out_3[0], in_1[0], in_2[0]);
  or or_2 (out_3[1], in_1[1], in_2[1]);
endmodule

module OR_8bit (
  input  [7:0] in_1,
  input  [7:0] in_2,
  output [7:0] out_3
);

  OR_2bit or_2bit_1 (.in_1(in_1[1:0]), .in_2(in_2[1:0]), .out_3(out_3[1:0]));
  OR_2bit or_2bit_2 (.in_1(in_1[3:2]), .in_2(in_2[3:2]), .out_3(out_3[3:2]));
  OR_2bit or_2bit_3 (.in_1(in_1[5:4]), .in_2(in_2[5:4]), .out_3(out_3[5:4]));
  OR_2bit or_2bit_4 (.in_1(in_1[7:6]), .in_2(in_2[7:6]), .out_3(out_3[7:6]));
endmodule

module OR_32bit (
  input  [31:0] in_1,
  input  [31:0] in_2,
  output [31:0] out_3
);

  OR_8bit or_8bit_1 (.in_1(in_1[7:0]), .in_2(in_2[7:0]), .out_3(out_3[7:0]));
  OR_8bit or_8bit_2 (.in_1(in_1[15:8]), .in_2(in_2[15:8]), .out_3(out_3[15:8]));
  OR_8bit or_8bit_3 (.in_1(in_1[23:16]), .in_2(in_2[23:16]), .out_3(out_3[23:16]));
  OR_8bit or_8bit_4 ();  // open: in_1, in_2, out_3
  OR_8bit or_8bit_5 (.in_1(in_1[31:24]), .in_2(in_2[31:24]), .out_3(out_3[31:24]));
endmodule

module XOR_2bit (
  input  [1:0] in_1,
  input  [1:0] in_2,
  output [1:0] out_3
);

  xor xor_1 (out_3[0], in_1[0], in_2[0]);
  xor xor_2 (out_3[1], in_1[1], in_2[1]);
endmodule

module XOR_8bit (
  input  [7:0] in_1,
  input  [7:0] in_2,
  output [7:0] out_3
);

  XOR_2bit xor_2bit_1 (.in_1(in_1[1:0]), .in_2(in_2[1:0]), .out_3(out_3[1:0]));
  XOR_2bit xor_2bit_2 (.in_1(in_1[3:2]), .in_2(in_2[3:2]), .out_3(out_3[3:2]));
  XOR_2bit xor_2bit_3 (.in_1(in_1[5:4]), .in_2(in_2[5:4]), .out_3(out_3[5:4]));
  XOR_2bit xor_2bit_4 (.in_1(in_1[7:6]), .in_2(in_2[7:6]), .out_3(out_3[7:6]));
endmodule

module XOR_32bit (
  input  [31:0] in_1,
  input  [31:0] in_2,
  output [31:0] out_3
);

  XOR_8bit xor_8bit_1 (.in_1(in_1[7:0]), .in_2(in_2[7:0]), .out_3(out_3[7:0]));
  XOR_8bit xor_8bit_2 (.in_1(in_1[15:8]), .in_2(in_2[15:8]), .out_3(out_3[15:8]));
  XOR_8bit xor_8bit_3 (.in_1(in_1[23:16]), .in_2(in_2[23:16]), .out_3(out_3[23:16]));
  XOR_8bit xor_8bit_4 (.in_1(in_1[31:24]), .in_2(in_2[31:24]), .out_3(out_3[31:24]));
endmodule

module slt (
  input  [31:0] in_1,
  input  [31:0] in_2,
  output [31:0] out_3
);

  wire comparator_1_lt, multiplexer_1_out;

  Comparator #(.width(32)) comparator_1 (.a(in_1), .b(in_2), .lt(comparator_1_lt));  // open: gt, eq
  Multiplexer #(.enable("false")) multiplexer_1 (
    .in0(1'b0), .in1(1'b1), .out(multiplexer_1_out), .sel(comparator_1_lt));
  assign out_3 = {{31{1'b0}}, multiplexer_1_out};  // Bit_Extender bit_extender_1
endmodule
