// Logisim project control_logic.circ as structural Verilog: 1 circuit, main circuit control_logic
module control_logic (
  input  [31:0] inst,
  input  BrEq,
  input  BrLt,
  output PCSel,
  output RegWEn,
  output [2:0] ImmSel,
  output BrUn,
  output ASel,
  output BSel,
  output [3:0] ALUSel,
  output [3:0] MemRW,
  output [1:0] WBSel,
  output CSRSel,
  output CSRWen
);

  wire and_1_out, and_2_out, and_3_out, and_4_out, and_5_out, and_6_out, and_7_out, and_8_out, and_9_out,
       and_10_out, and_11_out, and_12_out, and_13_out, and_14_out, and_15_out, and_17_out, and_18_out,
       and_19_out, and_20_out, and_21_out, and_22_out, and_23_out, and_24_out, and_25_out, AUIPC, B, CSRW, I,
       I_out, J, JALR, LOAD, LUI, not_1_out, not_2_out, not_3_out, not_4_out, not_5_out, not_6_out,
       not_7_out, not_8_out, not_9_out, not_10_out, or_1_out, or_6_out, or_8_out, or_10_out, R, S, U;
  wire [1:0] multiplexer_6_out;
  wire [2:0] multiplexer_4_out, multiplexer_5_out, multiplexer_9_out, multiplexer_12_out;
  wire [3:0] multiplexer_1_out, multiplexer_2_out, multiplexer_7_out, multiplexer_11_out, multiplexer_13_out,
       multiplexer_14_out, multiplexer_16_out, multiplexer_17_out;

  Multiplexer #(.enable("false"), .select(3), .width(4)) multiplexer_1 (
    .in0(4'b0000), .in1(4'b0110), .in2(4'b0111), .in3(4'b1011), .in4(4'b0011), .in5(4'b0100), .in6(4'b0010),
    .in7(4'b0001), .out(multiplexer_1_out), .sel(inst[14:12]));
  Multiplexer #(.enable("false"), .select(2), .width(4)) multiplexer_2 (
    .in0(4'b0001), .in1(4'b0011), .in2(4'b1111), .out(multiplexer_2_out), .sel(inst[13:12]));  // open: in3
  not not_1 (not_1_out, inst[12]);
  not not_2 (not_2_out, inst[13]);
  not not_3 (not_3_out, inst[14]);
  not not_4 (not_4_out, inst[6]);
  not not_5 (not_5_out, inst[5]);
  not not_6 (not_6_out, inst[4]);
  not not_7 (not_7_out, inst[3]);
  not not_8 (not_8_out, inst[2]);
  Multiplexer #(.enable("false"), .width(4)) multiplexer_3 (
    .in0(4'b0000), .in1(multiplexer_2_out), .out(MemRW), .sel(S));
  and and_1 (and_1_out, not_1_out, not_2_out, not_3_out);
  and and_2 (and_2_out, inst[12], not_2_out, inst[14]);
  and and_3 (and_3_out, inst[12], inst[13], not_3_out);
  and and_4 (and_4_out, inst[12], not_3_out, not_2_out);
  and and_5 (and_5_out, not_1_out, not_2_out, inst[14]);
  and and_6 (and_6_out, inst[12], not_2_out, inst[14]);
  and and_7 (and_7_out, not_1_out, inst[13], inst[14]);
  and and_8 (and_8_out, inst[12], inst[13], inst[14]);
  and and_9 (and_9_out, inst[30], and_1_out);
  and and_10 (and_10_out, inst[25], and_1_out);
  and and_11 (and_11_out, and_2_out, inst[30]);
  and and_12 (and_12_out, and_3_out, inst[25]);
  and and_13 (and_13_out, and_4_out, inst[25]);
  or or_1 (or_1_out, and_2_out, and_4_out);
  not not_9 (not_9_out, BrEq);
  not not_10 (not_10_out, BrLt);
  and u_load (LOAD, not_4_out, not_5_out, not_6_out, not_7_out, not_8_out);
  and u_I (I_out, not_4_out, not_5_out, inst[4], not_7_out, not_8_out);
  and u_S (S, not_4_out, inst[5], not_6_out, not_7_out, not_8_out);
  and u_B (B, inst[6], inst[5], not_6_out, not_7_out, not_8_out);
  and u_R (R, not_4_out, inst[5], inst[4], not_7_out, not_8_out);
  and u_AUIPC (AUIPC, not_4_out, not_5_out, inst[4], not_7_out, inst[2]);
  and u_LUI (LUI, not_4_out, inst[5], inst[4], not_7_out, inst[2]);
  and u_J (J, inst[6], inst[5], not_6_out, inst[3], inst[2]);
  and u_JALR (JALR, inst[6], inst[5], not_6_out, not_7_out, inst[2]);
  and u_CSRW (CSRW, inst[6], inst[5], inst[4], not_7_out, not_8_out);
  or or_2 (RegWEn, R, I, U, J);
  Multiplexer #(.enable("false"), .width(3)) multiplexer_4 (
    .in0(3'b000), .in1(3'b001), .out(multiplexer_4_out), .sel(S));
  Multiplexer #(.enable("false"), .width(3)) multiplexer_5 (
    .in0(multiplexer_4_out), .in1(3'b010), .out(multiplexer_5_out), .sel(B));
  Multiplexer #(.enable("false"), .width(2)) multiplexer_6 (
    .in0(2'b01), .in1(2'b00), .out(multiplexer_6_out), .sel(LOAD));
  Multiplexer #(.enable("false"), .width(4)) multiplexer_7 (
    .in0(multiplexer_1_out), .in1(4'b0101), .out(multiplexer_7_out), .sel(and_11_out));
  and and_14 (and_14_out, and_9_out, R);
  Multiplexer #(.enable("false")) multiplexer_8 (.in0(1'b0), .in1(1'b1), .out(CSRSel), .sel(and_15_out));
  and and_15 (and_15_out, and_2_out, CSRW);
  and and_16 (CSRWen, or_1_out, CSRW);
  and and_17 (and_17_out, and_1_out, BrEq);
  and and_18 (and_18_out, and_4_out, not_9_out);
  and and_19 (and_19_out, and_5_out, BrLt);
  and and_20 (and_20_out, and_6_out, not_10_out);
  and and_21 (and_21_out, and_7_out, BrLt);
  and and_22 (and_22_out, and_8_out, not_10_out);
  or or_3 (U, AUIPC, LUI);
  Multiplexer #(.enable("false"), .width(3)) multiplexer_9 (
    .in0(multiplexer_5_out), .in1(3'b011), .out(multiplexer_9_out), .sel(U));
  or or_4 (ASel, B, J, AUIPC);
  or or_5 (BSel, I, S, B, U, J);
  Multiplexer #(.enable("false"), .width(2)) multiplexer_10 (
    .in0(multiplexer_6_out), .in1(2'b10), .out(WBSel), .sel(or_6_out));
  or or_6 (or_6_out, J, JALR);
  Multiplexer #(.enable("false"), .width(4)) multiplexer_11 (
    .in0(multiplexer_7_out), .in1(4'b1100), .out(multiplexer_11_out), .sel(and_14_out));
  and and_23 (and_23_out, and_10_out, R);
  and and_24 (and_24_out, R, and_12_out);
  or or_7 (I, LOAD, I_out, JALR, CSRW);
  Multiplexer #(.enable("false"), .width(3)) multiplexer_12 (
    .in0(multiplexer_9_out), .in1(3'b100), .out(multiplexer_12_out), .sel(J));
  Multiplexer #(.enable("false"), .width(4)) multiplexer_13 (
    .in0(multiplexer_11_out), .in1(4'b1010), .out(multiplexer_13_out), .sel(and_23_out));
  Multiplexer #(.enable("false"), .width(4)) multiplexer_14 (
    .in0(multiplexer_13_out), .in1(4'b1011), .out(multiplexer_14_out), .sel(and_24_out));
  or or_8 (or_8_out, and_17_out, and_18_out, and_19_out, and_20_out, and_21_out, and_22_out);
  and and_25 (and_25_out, or_8_out, B);
  Multiplexer #(.enable("false"), .width(3)) multiplexer_15 (
    .in0(multiplexer_12_out), .in1(3'b101), .out(ImmSel), .sel(CSRW));
  Multiplexer #(.enable("false"), .width(4)) multiplexer_16 (
    .in0(multiplexer_14_out), .in1(4'b1110), .out(multiplexer_16_out), .sel(and_13_out));
  Multiplexer #(.enable("false"), .width(4)) multiplexer_17 (
    .in0(multiplexer_16_out), .in1(4'b1101), .out(multiplexer_17_out), .sel(U));
  or or_9 (PCSel, and_25_out, J, JALR);
  Multiplexer #(.enable("false"), .width(4)) multiplexer_18 (
    .in0(multiplexer_17_out), .in1(4'b0000), .out(ALUSel), .sel(or_10_out));
  or or_10 (or_10_out, JALR, LOAD, S, B, AUIPC, J);

  assign BrUn = inst[14];

  // Notes on the sheet:
  //   INPUTS to your circuit
  //   DON'T CHANGE THE LOCATIONS OF THE INPUTS AND OUTPUTS!
  //   OUTPUT from your circuit
endmodule
