// Logisim project cpu.circ as structural Verilog: 1 circuit, main circuit cpu
module cpu (
  input  clk,
  input  [31:0] INSTRUCTION,
  input  [31:0] READ_DATA,
  output [31:0] WRITE_ADDRESS,
  output [31:0] PROGRAM_COUNTER,
  output [31:0] ra,
  output [31:0] sp,
  output [31:0] t0,
  output [31:0] t1,
  output [31:0] t2,
  output [31:0] s0,
  output [31:0] s1,
  output [31:0] a0,
  output [31:0] tohost,
  output [3:0] WRITE_ENABLE,
  output [31:0] WRITE_DATA
);

  wire branch_comp_1_breq, branch_comp_1_brlt, control_logic_1_asel, control_logic_1_brun,
       control_logic_1_bsel, control_logic_1_csrsel, control_logic_1_csrwen, control_logic_1_pcsel,
       control_logic_1_regwen;
  wire [1:0] control_logic_1_wbsel;
  wire [2:0] control_logic_1_immsel;
  wire [3:0] control_logic_1_alusel;
  wire [11:0] register_2_q_2;
  wire [19:0] register_2_q;
  wire [31:0] adder_1_out, adder_2_out, bit_extender_1_out, bit_extender_2_out, imm_gen_1_imm,
       multiplexer_1_out, multiplexer_2_out, multiplexer_3_out, multiplexer_4_out, multiplexer_5_out,
       multiplexer_6_out, multiplexer_7_out, regfile_1_read_data_1, register_1_q;

  Adder #(.width(32)) adder_1 (.a(PROGRAM_COUNTER), .b(32'h4), .out(adder_1_out));  // open: cin, cout
  Multiplexer #(.enable("false"), .width(32)) multiplexer_1 (
    .in0(adder_1_out), .in1(WRITE_ADDRESS), .out(multiplexer_1_out), .sel(control_logic_1_pcsel));
  Register #(.width(32)) PC (.D(multiplexer_1_out), .clk(clk), .Q(PROGRAM_COUNTER));  // open: en, clr
  Multiplexer #(.enable("false"), .width(32)) multiplexer_2 (
    .in0(INSTRUCTION), .in1(32'h13), .out(multiplexer_2_out), .sel(control_logic_1_pcsel));
  Register #(.width(32)) register_1 (.D(PROGRAM_COUNTER), .clk(clk), .Q(register_1_q));  // open: en, clr
  Register #(.width(32)) register_2 (
    .D(multiplexer_2_out), .clk(clk), .Q({register_2_q_2, register_2_q}));  // open: en, clr
  control_logic control_logic_1 (
    .CSRWen(control_logic_1_csrwen), .PCSel(control_logic_1_pcsel), .RegWEn(control_logic_1_regwen),
    .ImmSel(control_logic_1_immsel), .BrUn(control_logic_1_brun), .ASel(control_logic_1_asel),
    .BSel(control_logic_1_bsel), .ALUSel(control_logic_1_alusel), .MemRW(WRITE_ENABLE),
    .WBSel(control_logic_1_wbsel), .CSRSel(control_logic_1_csrsel), .inst({register_2_q_2, register_2_q}),
    .BrEq(branch_comp_1_breq), .BrLt(branch_comp_1_brlt));
  regfile regfile_1 (
    .rs1(register_2_q[19:15]), .rs2(register_2_q_2[4:0]), .rd(register_2_q[11:7]),
    .Write_Data(multiplexer_5_out), .RegWEn(control_logic_1_regwen), .clk(clk), .ra(ra), .sp(sp), .t0(t0),
    .t1(t1), .t2(t2), .s0(s0), .s1(s1), .a0(a0), .Read_Data_1(regfile_1_read_data_1), .Read_Data_2(WRITE_DATA));
  imm_gen imm_gen_1 (.inst({register_2_q_2, register_2_q}), .ImmSel(control_logic_1_immsel), .imm(imm_gen_1_imm));
  Multiplexer #(.enable("false"), .width(32)) multiplexer_3 (
    .in0(regfile_1_read_data_1), .in1(register_1_q), .out(multiplexer_3_out), .sel(control_logic_1_asel));
  Multiplexer #(.enable("false"), .width(32)) multiplexer_4 (
    .in0(WRITE_DATA), .in1(imm_gen_1_imm), .out(multiplexer_4_out), .sel(control_logic_1_bsel));
  Multiplexer #(.enable("false"), .select(2), .width(32)) multiplexer_5 (
    .in0(multiplexer_6_out), .in1(WRITE_ADDRESS), .in2(adder_2_out), .out(multiplexer_5_out),
    .sel(control_logic_1_wbsel));  // open: in3
  branch_comp branch_comp_1 (
    .rs1(regfile_1_read_data_1), .rs2(WRITE_DATA), .BrUn(control_logic_1_brun), .BrEq(branch_comp_1_breq),
    .BrLt(branch_comp_1_brlt));
  assign bit_extender_1_out = {{24{READ_DATA[7]}}, READ_DATA[7:0]};  // Bit_Extender bit_extender_1
  assign bit_extender_2_out = {{16{READ_DATA[15]}}, READ_DATA[15:0]};  // Bit_Extender bit_extender_2
  alu alu_1 (.Result(WRITE_ADDRESS), .A(multiplexer_3_out), .B(multiplexer_4_out), .ALUSel(control_logic_1_alusel));
  Multiplexer #(.enable("false"), .select(2), .width(32)) multiplexer_6 (
    .in0(bit_extender_1_out), .in1(bit_extender_2_out), .in2(READ_DATA), .out(multiplexer_6_out),
    .sel(register_2_q[13:12]));  // open: in3
  Multiplexer #(.enable("false"), .width(32)) multiplexer_7 (
    .in0(regfile_1_read_data_1), .in1(imm_gen_1_imm), .out(multiplexer_7_out), .sel(control_logic_1_csrsel));
  Adder #(.width(32)) adder_2 (.a(register_1_q), .b(32'h4), .out(adder_2_out));  // open: cin, cout
  csr csr_1 (
    .CSR_address(register_2_q_2), .CSR_din(multiplexer_7_out), .CSR_WE(control_logic_1_csrwen), .clk(clk),
    .tohost(tohost));

  // Other names for the same wires on the sheet: BRANCH_JUMP_PC[31:0] = WRITE_ADDRESS

  // Notes on the sheet:
  //   Output to IMEM
  //   IMEM (do **NOT** move this)
  //   Inputs from IMEM
  //   It is OK to move the PC, RegFile, ALU, MEM, Branch Comp, Imm Gen, and Control Logic to wherever is most convenient for you when constructing your CPU, and to delete this text
  //   Inputs/Outputs for testing. Do **NOT** move these.
  //   Outputs To DMEM
  //   DMEM (do **NOT** move this)
  //   Inputs From DMEM
endmodule
