// Logisim project csr.circ as structural Verilog: 1 circuit, main circuit csr
module csr (
  input  [11:0] CSR_address,
  input  [31:0] CSR_din,
  input  CSR_WE,
  input  clk,
  output [31:0] tohost
);

  wire comparator_1_eq;
  wire [31:0] demultiplexer_1_out1;

  Comparator #(.mode("unsigned"), .width(12)) comparator_1 (
    .a(CSR_address), .b(12'h51e), .eq(comparator_1_eq));  // open: gt, lt
  Demultiplexer #(.enable("false"), .width(32)) demultiplexer_1 (
    .out1(demultiplexer_1_out1), .in(CSR_din), .sel(comparator_1_eq));  // open: out0
  Register #(.width(32)) register_1 (.D(demultiplexer_1_out1), .en(CSR_WE), .clk(clk), .Q(tohost));  // open: clr

  // Other names for the same wires on the sheet: address[11:0] = CSR_address; data[31:0] = CSR_din; WE = CSR_WE

  // Notes on the sheet:
  //   INPUTS to your circuit
  //   DON'T CHANGE THE LOCATIONS OF THE INPUTS AND OUTPUTS!
  //   OUTPUT from your circuit
endmodule
